// Logisim project lab2_adv.circ as structural Verilog
module multiplier (
  input  [3:0] a,
  input  [3:0] b,
  output [7:0] p
);

  wire [2:0] and_2_out;
  wire [3:0] and_5_out, and_9_out, and_13_out;
  wire [3:1] adder_1_out, adder_2_out;
  wire [3:3] adder_1_cout, adder_2_cout;

  and and_1 (p[0], a[0], b[0]);
  and and_2 (and_2_out[0], a[1], b[0]);
  and and_3 (and_2_out[1], a[2], b[0]);
  and and_4 (and_2_out[2], a[3], b[0]);
  and and_5 (and_5_out[0], a[0], b[1]);
  and and_6 (and_5_out[1], a[1], b[1]);
  and and_7 (and_5_out[2], a[2], b[1]);
  and and_8 (and_5_out[3], a[3], b[1]);
  and and_9 (and_9_out[0], a[0], b[2]);
  and and_10 (and_9_out[1], a[1], b[2]);
  and and_11 (and_9_out[2], a[2], b[2]);
  and and_12 (and_9_out[3], a[3], b[2]);
  and and_13 (and_13_out[0], a[0], b[3]);
  and and_14 (and_13_out[1], a[1], b[3]);
  and and_15 (and_13_out[2], a[2], b[3]);
  and and_16 (and_13_out[3], a[3], b[3]);
  Adder #(.width(4)) adder_1 (
    .a({1'b0, and_2_out}), .b(and_5_out), .out({adder_1_out, p[1]}), .cout(adder_1_cout[3]));  // open: cin
  Adder #(.width(4)) adder_2 (
    .a({adder_1_cout[3], adder_1_out}), .b(and_9_out), .out({adder_2_out, p[2]}), .cout(adder_2_cout[3]));  // open: cin
  Adder #(.width(4)) adder_3 (
    .a({adder_2_cout[3], adder_2_out}), .b(and_13_out), .out(p[6:3]), .cout(p[7]));  // open: cin
endmodule

module Universal_Gate (
  input  a,
  input  b,
  output c
);

  wire not_1_out;

  and and_1 (c, a, not_1_out);
  not not_1 (not_1_out, b);
endmodule

module ug_not (
  input  in_1,
  output out_2
);

  Universal_Gate Universal_Gate (.a(1'b1), .b(in_1), .c(out_2));
endmodule

module ug_and (
  input  in_1,
  input  in_2,
  output out_3
);

  wire ug_not_out_2;

  Universal_Gate Universal_Gate (.a(in_1), .b(ug_not_out_2), .c(out_3));
  ug_not ug_not (.in_1(in_2), .out_2(ug_not_out_2));
endmodule

module ug_or (
  input  in_1,
  input  in_2,
  output out_3
);

  wire ug_not_out_2, Universal_Gate_c;

  ug_not ug_not (.in_1(in_1), .out_2(ug_not_out_2));
  Universal_Gate Universal_Gate (.a(ug_not_out_2), .b(in_2), .c(Universal_Gate_c));
  ug_not ug_not_2 (.in_1(Universal_Gate_c), .out_2(out_3));
endmodule

module ug_xor (
  input  in_1,
  input  in_2,
  output out_3
);

  wire ug_and_2_out_3, ug_and_out_3, ug_not_out_2;

  ug_not ug_not (.in_1(in_1), .out_2(ug_not_out_2));
  ug_and ug_and (.in_1(ug_not_out_2), .in_2(in_2), .out_3(ug_and_out_3));
  ug_and ug_and_2 (.in_1(in_1), .in_2(in_1), .out_3(ug_and_2_out_3));
  ug_not ug_not_2 (.in_1(in_2), .out_2(in_1));
  ug_or ug_or_1 (.in_1(ug_and_out_3), .in_2(ug_and_2_out_3), .out_3(out_3));
endmodule

module ug_xnor (
  input  in_1,
  input  in_2,
  output out_3
);

  wire ug_and_2_out_3, ug_and_out_3, ug_not_2_out_2, ug_not_out_2;

  ug_not ug_not (.in_1(in_2), .out_2(ug_not_out_2));
  ug_and ug_and (.in_1(in_1), .in_2(in_2), .out_3(ug_and_out_3));
  ug_not ug_not_2 (.in_1(in_1), .out_2(ug_not_2_out_2));
  ug_and ug_and_2 (.in_1(ug_not_2_out_2), .in_2(ug_not_out_2), .out_3(ug_and_2_out_3));
  // ug_or ug_or_1: pin names not known; wires that end beside it: ug_and_out_3, ug_and_2_out_3, out_3
endmodule

module half_adder (
);

  nand_xor nand_xor ();
  nand_and nand_and ();
endmodule

module adder (
  input  in_1,
  input  in_2,
  input  cin,
  output cout,
  output sum
);

  wire undriven, undriven_2;

  half_adder half_adder ();
  half_adder half_adder_2 ();
  or or_1 (cout, undriven, undriven_2);
endmodule

module adder4bit (
  input  [3:0] in_1,
  input  [3:0] in_2,
  output [3:0] sum,
  output cout
);

  wire adder_2_cout, adder_3_cout, adder_cout;

  adder adder (.in_1(in_1[0]), .in_2(in_2[0]), .cin(1'b0), .cout(adder_cout), .sum(sum[0]));
  adder adder_2 (.in_1(in_1[1]), .in_2(in_2[1]), .cin(adder_cout), .cout(adder_2_cout), .sum(sum[1]));
  adder adder_3 (.in_1(in_1[2]), .in_2(in_2[2]), .cin(adder_2_cout), .cout(adder_3_cout), .sum(sum[2]));
  adder adder_4 (.in_1(in_1[3]), .in_2(in_2[3]), .cin(adder_3_cout), .cout(cout), .sum(sum[3]));
endmodule

module complementer4bit (
  input  [3:0] in_1,
  output [3:0] out_2
);

  wire [3:0] ug_not_out_2;

  ug_not ug_not (.in_1(in_1[0]), .out_2(ug_not_out_2[0]));
  ug_not ug_not_2 (.in_1(in_1[1]), .out_2(ug_not_out_2[1]));
  ug_not ug_not_3 (.in_1(in_1[2]), .out_2(ug_not_out_2[2]));
  ug_not ug_not_4 (.in_1(in_1[3]), .out_2(ug_not_out_2[3]));
  adder4bit adder4bit (.in_1(ug_not_out_2), .in_2(4'b0001), .sum(out_2));  // open: cout
endmodule

module suber4bit (
  input  [3:0] a,
  input  [3:0] b,
  output [3:0] dif
);

  wire [3:0] complementer4bit_out_2;

  complementer4bit complementer4bit (.in_1(b), .out_2(complementer4bit_out_2));
  adder4bit adder4bit (.in_1(a), .in_2(complementer4bit_out_2), .sum(dif));  // open: cout
endmodule

module ari_r_shift (
  input  [3:0] in_1,
  output [3:0] out_2
);


  assign out_2 = {{2{in_1[3]}}, in_1[2:1]};
endmodule

module cir_l_shift (
  input  [3:0] in_1,
  output [3:0] out_2
);


  assign in_1[2:0] = {3{in_1[3]}};
  assign out_2 = {4{in_1[3]}};
endmodule

module mux (
  input  [3:0] in_1,
  input  [3:0] in_2,
  input  sel,
  output [3:0] out_4
);

  wire [3:0] and_1_out, and_2_out, not_1_out;

  assign not_1_out = ~{4{sel}};  // NOT_Gate not_1, 4 bits wide
  assign and_1_out = in_1 & not_1_out;  // AND_Gate and_1, 4 bits wide
  assign and_2_out = in_2 & {4{sel}};  // AND_Gate and_2, 4 bits wide
  assign out_4 = and_1_out | and_2_out;  // OR_Gate or_1, 4 bits wide
endmodule

module mux8 (
  input  [3:0] in_1,
  input  [3:0] in_2,
  input  [3:0] in_3,
  input  [3:0] in_4,
  input  [3:0] in_5,
  input  [3:0] in_6,
  input  [3:0] in_7,
  input  [3:0] in_8,
  input  [2:0] sel,
  output [3:0] out_10
);

  wire [3:0] multiplexer_1_out, multiplexer_2_out, multiplexer_3_out, multiplexer_4_out, multiplexer_5_out,
       multiplexer_6_out;

  Multiplexer #(.width(4), .enable("false")) multiplexer_1 (
    .in0(in_1), .in1(in_2), .out(multiplexer_1_out), .sel(sel[0]));
  Multiplexer #(.width(4), .enable("false")) multiplexer_2 (
    .in0(in_3), .in1(in_4), .out(multiplexer_2_out), .sel(sel[0]));
  Multiplexer #(.width(4), .enable("false")) multiplexer_3 (
    .in0(in_5), .in1(in_6), .out(multiplexer_3_out), .sel(sel[0]));
  Multiplexer #(.width(4), .enable("false")) multiplexer_4 (
    .in0(in_7), .in1(in_8), .out(multiplexer_4_out), .sel(sel[0]));
  Multiplexer #(.width(4), .enable("false")) multiplexer_5 (
    .in0(multiplexer_1_out), .in1(multiplexer_2_out), .out(multiplexer_5_out), .sel(sel[1]));
  Multiplexer #(.width(4), .enable("false")) multiplexer_6 (
    .in0(multiplexer_3_out), .in1(multiplexer_4_out), .out(multiplexer_6_out), .sel(sel[1]));
  Multiplexer #(.width(4), .enable("false")) multiplexer_7 (
    .in0(multiplexer_5_out), .in1(multiplexer_6_out), .out(out_10), .sel(sel[2]));
endmodule

module comparator (
  input  [3:0] a,
  input  [3:0] b,
  output [3:0] eq,
  output [3:0] le
);

  wire and_3_out, and_4_out, and_5_out;
  wire [3:0] and_1_out, not_1_out, xnor_1_out;

  assign xnor_1_out = ~(a ^ b);  // XNOR_Gate xnor_1, 4 bits wide
  assign not_1_out = ~a;  // NOT_Gate not_1, 4 bits wide
  assign and_1_out = not_1_out & b;  // AND_Gate and_1, 4 bits wide
  and and_2 (eq[0], xnor_1_out[0], xnor_1_out[1], xnor_1_out[2], xnor_1_out[3]);
  and and_3 (and_3_out, xnor_1_out[1], xnor_1_out[2], xnor_1_out[3], and_1_out[0]);
  and and_4 (and_4_out, and_1_out[1], xnor_1_out[2], xnor_1_out[3]);
  and and_5 (and_5_out, xnor_1_out[3], and_1_out[2]);
  or or_1 (le[0], and_3_out, and_4_out, and_5_out, and_1_out[3]);

  assign eq[3:1] = 3'b111;
  assign le[3:1] = 3'b101;
endmodule

module Decode_And_Execute (
  input  [3:0] rs,
  input  [3:0] rt,
  input  [2:0] sel,
  output [3:0] rd
);

  wire [3:0] adder4bit_sum, and_1_out, ari_r_shift_out_2, cir_l_shift_out_2, comparator_eq, comparator_le,
       or_1_out, suber4bit_dif;

  assign or_1_out = rs | rt;  // OR_Gate or_1, 4 bits wide
  assign and_1_out = rs & rt;  // AND_Gate and_1, 4 bits wide
  suber4bit suber4bit (.a(rs), .b(rt), .dif(suber4bit_dif));
  adder4bit adder4bit (.in_1(rs), .in_2(rt), .sum(adder4bit_sum));  // open: cout
  ari_r_shift ari_r_shift (.in_1(rt), .out_2(ari_r_shift_out_2));
  cir_l_shift cir_l_shift (.in_1(rs), .out_2(cir_l_shift_out_2));
  comparator comparator (.a(rs), .b(rt), .eq(comparator_eq), .le(comparator_le));
  Multiplexer #(.select(3), .width(4), .enable("false")) multiplexer_1 (
    .in0(suber4bit_dif), .in1(adder4bit_sum), .in2(or_1_out), .in3(and_1_out), .in4(ari_r_shift_out_2),
    .in5(cir_l_shift_out_2), .in6(comparator_le), .in7(comparator_eq), .out(rd), .sel(sel));
endmodule

module nand_and (
);

  wire input_a, input_b, nand_1_out, \output ;

  nand nand_1 (nand_1_out, input_a, input_b);
  nand nand_2 (\output , nand_1_out, nand_1_out);
endmodule

module nand_or (
);

  wire input_a, input_b, nand_1_out, nand_2_out, \output ;

  nand nand_1 (nand_1_out, input_a, input_a);
  nand nand_2 (nand_2_out, input_b, input_b);
  nand nand_3 (\output , nand_1_out, nand_2_out);
endmodule

module nand_not (
);

  wire \input , \output ;

  nand nand_1 (\output , \input , \input );
endmodule

module nand_xor (
);

  nand_not nand_not ();
  nand_not nand_not_2 ();
  nand_and nand_and ();
  nand_and nand_and_2 ();
  nand_or nand_or ();
endmodule

module nand_nor (
);

  nand_or nand_or ();
  nand_not nand_not ();
endmodule

module nand_xnor (
);

  nand_not nand_not ();
  nand_not nand_not_2 ();
  nand_and nand_and ();
  nand_and nand_and_2 ();
  nand_or nand_or ();
endmodule

module basic_1 (
);

  wire input_a, input_b, multiplexer_1_out, multiplexer_2_out, multiplexer_3_out, multiplexer_4_out,
       multiplexer_5_out, multiplexer_6_out, nand_1_out, out, sel_0, sel_1, sel_2, undriven, undriven_2,
       undriven_3, undriven_4, undriven_5, undriven_6;

  nand_and nand_and ();
  nand_or nand_or ();
  nand_nor nand_nor ();
  nand_xor nand_xor ();
  nand_xnor nand_xnor ();
  nand_not nand_not ();
  nand nand_1 (nand_1_out, input_a, input_b);
  Multiplexer multiplexer_1 (.in0(nand_1_out), .in1(undriven_3), .out(multiplexer_1_out), .sel(sel_0));  // open: en
  Multiplexer multiplexer_2 (.in0(undriven), .in1(undriven_4), .out(multiplexer_2_out), .sel(sel_0));  // open: en
  Multiplexer multiplexer_3 (.in0(undriven_2), .in1(undriven_5), .out(multiplexer_3_out), .sel(sel_0));  // open: en
  Multiplexer multiplexer_4 (.in0(undriven_6), .in1(undriven_6), .out(multiplexer_4_out), .sel(sel_0));  // open: en
  Multiplexer multiplexer_5 (
    .in0(multiplexer_1_out), .in1(multiplexer_2_out), .out(multiplexer_5_out), .sel(sel_1));  // open: en
  Multiplexer multiplexer_6 (
    .in0(multiplexer_3_out), .in1(multiplexer_4_out), .out(multiplexer_6_out), .sel(sel_1));  // open: en
  Multiplexer multiplexer_7 (.in0(multiplexer_5_out), .in1(multiplexer_6_out), .out(out), .sel(sel_2));  // open: en
endmodule

module full_adder (
);

  nand_xor nand_xor ();
  nand_and nand_and ();
  nand_and nand_and_2 ();
  nand_and nand_and_3 ();
  nand_xor nand_xor_2 ();
  nand_or nand_or ();
  nand_or nand_or_2 ();
endmodule

module RCA (
);

  full_adder full_adder ();
  full_adder full_adder_2 ();
  full_adder full_adder_3 ();
  full_adder full_adder_4 ();
  full_adder full_adder_5 ();

  // Notes on the sheet:
  //      C2
  //   C1
  //   C7
endmodule

module CLA_4bit (
);

  nand_and nand_and ();
  nand_or nand_or ();
  nand_and nand_and_2 ();
  nand_and nand_and_3 ();
  nand_or nand_or_2 ();
  nand_and nand_and_4 ();
  nand_and nand_and_5 ();
  nand_and nand_and_6 ();
  nand_or nand_or_3 ();
  nand_or nand_or_4 ();
  nand_or nand_or_5 ();
  nand_and nand_and_7 ();
  nand_and nand_and_8 ();
  nand_and nand_and_9 ();
  nand_or nand_or_6 ();
  nand_or nand_or_7 ();
  nand_or nand_or_8 ();
  nand_or nand_or_9 ();
  nand_and nand_and_10 ();
  nand_and nand_and_11 ();
  nand_and nand_and_12 ();
endmodule

module CLA_2bit (
);

  nand_and nand_and ();
  nand_or nand_or ();
  nand_and nand_and_2 ();
  nand_or nand_or_2 ();
endmodule

module getpgs (
);

  nand_xor nand_xor ();
  nand_and nand_and ();
  nand_or nand_or ();
  nand_xor nand_xor_2 ();
endmodule
