// Logisim project lab3_adv.circ as structural Verilog
module FIFO_8 (
  input  clk,
  input  rst_n,
  input  wen,
  input  ren,
  input  [7:0] din,
  output [7:0] dout,
  output error
);

  wire and_2_out, and_3_out, and_4_out, empty_out, full_out, multiplexer_6_out, nand_1_out, not_1_out,
       not_2_out, not_3_out, not_4_out, not_5_out, or_1_out;
  wire [2:0] adder_1_out, adder_2_out, adder_3_out, and_1_out, and_5_out, and_6_out, back_q, front_q,
       multiplexer_1_out, multiplexer_3_out, multiplexer_4_out, multiplexer_7_out, multiplexer_8_out,
       xnor_1_out, xnor_2_out;
  wire [7:0] multiplexer_2_out, multiplexer_5_out, ram_1_data, undriven;

  not not_1 (not_1_out, wen);
  nand nand_1 (nand_1_out, not_1_out, ren, full_out);
  not not_2 (not_2_out, empty_out);
  not not_3 (not_3_out, rst_n);
  Adder #(.width(3)) adder_1 (.a(front_q), .b(3'b001), .out(adder_1_out));  // open: cin, cout
  assign and_1_out = adder_1_out & 3'b111;  // AND_Gate and_1, 3 bits wide
  and and_2 (and_2_out, rst_n, empty_out);
  or or_1 (or_1_out, and_2_out, and_3_out);
  and and_3 (and_3_out, not_3_out, wen, full_out);
  Adder #(.width(3)) adder_2 (.a(back_q), .b(3'b001), .out(adder_2_out));  // open: cin, cout
  Multiplexer #(.width(3), .enable("false")) multiplexer_1 (
    .in0(front_q), .in1(and_1_out), .out(multiplexer_1_out), .sel(and_4_out));
  and and_4 (and_4_out, not_2_out, ren);
  Multiplexer #(.width(8), .enable("false")) multiplexer_2 (
    .in0(undriven), .out(multiplexer_2_out), .sel(nand_1_out));  // open: in1
  Multiplexer #(.width(3), .enable("false")) multiplexer_3 (
    .in0(back_q), .in1(and_5_out), .out(multiplexer_3_out), .sel(nand_1_out));
  assign and_5_out = adder_2_out & 3'b111;  // AND_Gate and_5, 3 bits wide
  Multiplexer #(.width(3), .enable("false")) multiplexer_4 (
    .in0(multiplexer_1_out), .in1(3'b000), .out(multiplexer_4_out), .sel(rst_n));
  Register #(.width(3)) front (.D(multiplexer_4_out), .Q(front_q), .clk(clk));  // open: en, clr
  Multiplexer #(.width(8), .enable("false")) multiplexer_5 (
    .in0(multiplexer_2_out), .in1({8{1'b0}}), .out(multiplexer_5_out), .sel(rst_n));
  Register out (.D(multiplexer_5_out), .Q(dout), .clk(clk));  // open: en, clr
  Multiplexer #(.enable("false")) multiplexer_6 (.in0(or_1_out), .in1(1'b0), .out(multiplexer_6_out), .sel(rst_n));
  Multiplexer #(.width(3), .enable("false")) multiplexer_7 (
    .in0(and_5_out), .in1(and_1_out), .out(multiplexer_7_out), .sel(ren));
  Multiplexer #(.width(3), .enable("false")) multiplexer_8 (
    .in0(multiplexer_3_out), .in1(3'b000), .out(multiplexer_8_out), .sel(rst_n));
  Register #(.width(3)) back (.D(multiplexer_8_out), .Q(back_q), .clk(clk));  // open: en, clr
  Register #(.width(1)) err (.D(multiplexer_6_out), .Q(error), .clk(clk));  // open: en, clr
  not not_4 (not_4_out, ren);
  Adder #(.width(3)) adder_3 (.a(back_q), .b(3'b001), .out(adder_3_out));  // open: cin, cout
  RAM #(.addrWidth(3)) ram_1 (.addr(multiplexer_7_out), .data(ram_1_data), .ld(not_4_out));  // open: sel, clk, clr
  Multiplexer #(.width(8), .enable("false")) multiplexer_9 (.in0(undriven), .in1(din), .out(ram_1_data), .sel(ren));
  assign and_6_out = adder_3_out & 3'b111;  // AND_Gate and_6, 3 bits wide
  assign xnor_1_out = ~(back_q ^ front_q);  // XNOR_Gate xnor_1, 3 bits wide
  assign xnor_2_out = ~(and_6_out ^ front_q);  // XNOR_Gate xnor_2, 3 bits wide
  and full (full_out, xnor_2_out[0], xnor_2_out[1], xnor_2_out[2]);
  not not_5 (not_5_out, full_out);
  and empty (empty_out, not_5_out, xnor_1_out[0], xnor_1_out[1], xnor_1_out[2]);
endmodule

module Round_Robin_FIFO_Arbiter (
  input  rst_n,
  input  [3:0] wen,
  input  [7:0] a,
  input  [7:0] b,
  input  [7:0] c,
  input  [7:0] d,
  output [7:0] dout,
  output valid
);

  wire and_1_out, and_2_out, and_3_out, and_4_out, and_5_out, and_7_out, and_8_out, clk_out, decoder_1_out0,
       decoder_1_out1, decoder_1_out2, decoder_1_out3, multiplexer_4_out, not_1_out, not_3_out, qa_error,
       qb_error, qc_error, qd_error, ra_q, rb_q, rc_q, rd_q;
  wire [1:0] cnt_q;
  wire [3:0] dwren_q, multiplexer_1_out, not_2_out;
  wire [7:0] multiplexer_2_out, multiplexer_3_out, qa_dout, qb_dout, qc_dout, qd_dout;

  not not_1 (not_1_out, rst_n);
  Multiplexer #(.width(4), .enable("false")) multiplexer_1 (
    .in0(wen), .in1(4'b1111), .out(multiplexer_1_out), .sel(rst_n));
  Decoder #(.select(2)) decoder_1 (
    .out0(decoder_1_out0), .out1(decoder_1_out1), .out2(decoder_1_out2), .out3(decoder_1_out3), .sel(cnt_q));  // open: en
  Counter #(.width(2), .max('h3), .ongoal("continue")) cnt (
    .load(not_1_out), .D(2'b00), .count(rst_n), .Q(cnt_q), .clk(clk_out));  // open: carry, clr
  Register #(.width(4)) dwren (.D(multiplexer_1_out), .Q(dwren_q), .clk(clk_out));  // open: en, clr
  Clock clk (.out(clk_out));
  assign not_2_out = ~wen;  // NOT_Gate not_2, 4 bits wide
  and and_1 (and_1_out, not_2_out[0], decoder_1_out0);
  Register #(.width(1)) ra (.D(and_1_out), .Q(ra_q), .clk(clk_out));  // open: en, clr
  and and_2 (and_2_out, not_2_out[1], decoder_1_out1);
  and and_3 (and_3_out, not_2_out[2], decoder_1_out2);
  and and_4 (and_4_out, not_2_out[3], decoder_1_out3);
  FIFO_8 qa (.clk(clk_out), .rst_n(rst_n), .wen(wen[0]), .ren(ra_q), .din(a), .dout(qa_dout), .error(qa_error));
  Register #(.width(1)) rb (.D(and_2_out), .Q(rb_q), .clk(clk_out));  // open: en, clr
  and and_5 (and_5_out, qa_error, dwren_q[0]);
  FIFO_8 qb (.clk(clk_out), .rst_n(rst_n), .wen(wen[1]), .ren(rb_q), .din(b), .dout(qb_dout), .error(qb_error));
  and and_6 (and_5_out, qb_error, dwren_q[1]);
  FIFO_8 qc (.clk(clk_out), .rst_n(rst_n), .wen(wen[2]), .ren(rc_q), .din(c), .dout(qc_dout), .error(qc_error));
  Register #(.width(1)) rc (.D(and_3_out), .Q(rc_q), .clk(clk_out));  // open: en, clr
  FIFO_8 qd (.clk(clk_out), .rst_n(rst_n), .wen(wen[3]), .ren(rd_q), .din(d), .dout(qd_dout), .error(qd_error));
  Register #(.width(1)) rd (.D(and_4_out), .Q(rd_q), .clk(clk_out));  // open: en, clr
  and and_7 (and_7_out, qc_error, dwren_q[2]);
  and and_8 (and_8_out, qd_error, dwren_q[3]);
  Multiplexer #(.width(8), .enable("false")) multiplexer_2 (
    .in0({8{1'b0}}), .in1(multiplexer_3_out), .out(multiplexer_2_out), .sel(not_3_out));
  Multiplexer #(.select(2), .width(8), .enable("false")) multiplexer_3 (
    .in0(qa_dout), .in1(qb_dout), .in2(qc_dout), .in3(qd_dout), .out(multiplexer_3_out), .sel(cnt_q));
  Multiplexer #(.select(2), .enable("false")) multiplexer_4 (
    .in0(and_5_out), .in1(and_5_out), .in2(and_7_out), .in3(and_8_out), .out(multiplexer_4_out), .sel(cnt_q));
  not not_3 (not_3_out, multiplexer_4_out);
  Register out (.D(multiplexer_2_out), .Q(dout), .clk(clk_out));  // open: en, clr
  Register #(.width(1)) vld (.D(not_3_out), .Q(valid), .clk(clk_out));  // open: en, clr
endmodule

module Bank (
  input  clk,
  input  ren,
  input  wen,
  input  [8:0] raddr,
  input  [8:0] waddr,
  input  [7:0] din,
  output [7:0] dout
);

  wire and_1_out, decoder_1_out0, decoder_1_out1, decoder_1_out2, decoder_1_out3, decoder_2_out0,
       decoder_2_out1, decoder_2_out2, decoder_2_out3, dren_q, multiplexer_2_out, multiplexer_3_out,
       multiplexer_5_out, multiplexer_7_out, multiplexer_8_out, multiplexer_9_out, multiplexer_11_out,
       multiplexer_12_out, nand_1_out, ra_q, rb_q, rc_q, rd_q, wa_q, wb_q, wc_q, wd_q;
  wire [1:0] drmem_q, xnor_1_out;
  wire [6:0] addra_q, addrb_q, addrc_q, addrd_q, multiplexer_1_out, multiplexer_4_out, multiplexer_6_out,
       multiplexer_10_out;
  wire [7:0] multiplexer_17_out, ram_1_data, ram_2_data, ram_3_data, ram_4_data, undriven, undriven_2,
       undriven_3, undriven_4;

  Decoder #(.select(2), .enable("false")) decoder_1 (
    .out0(decoder_1_out0), .out1(decoder_1_out1), .out2(decoder_1_out2), .out3(decoder_1_out3),
    .sel(raddr[8:7]));
  Decoder #(.select(2), .enable("false")) decoder_2 (
    .out0(decoder_2_out0), .out1(decoder_2_out1), .out2(decoder_2_out2), .out3(decoder_2_out3),
    .sel(waddr[8:7]));
  assign xnor_1_out = ~(raddr[8:7] ^ waddr[8:7]);  // XNOR_Gate xnor_1, 2 bits wide
  Multiplexer #(.width(7), .enable("false")) multiplexer_1 (
    .in0(waddr[6:0]), .in1(raddr[6:0]), .out(multiplexer_1_out), .sel(decoder_1_out0));
  Multiplexer #(.enable("false")) multiplexer_2 (.in0(1'b0), .in1(decoder_1_out0), .out(multiplexer_2_out), .sel(ren));
  nand nand_1 (nand_1_out, ren, xnor_1_out[0], xnor_1_out[1]);
  Register #(.width(7)) addra (.D(multiplexer_1_out), .Q(addra_q), .clk(clk));  // open: en, clr
  Register #(.width(1)) ra (.D(multiplexer_2_out), .Q(ra_q), .clk(clk));  // open: en, clr
  Multiplexer #(.enable("false")) multiplexer_3 (
    .in0(1'b0), .in1(decoder_2_out0), .out(multiplexer_3_out), .sel(and_1_out));
  and and_1 (and_1_out, wen, nand_1_out);
  Register #(.width(7)) addrb (.D(multiplexer_4_out), .Q(addrb_q), .clk(clk));  // open: en, clr
  Multiplexer #(.width(7), .enable("false")) multiplexer_4 (
    .in0(waddr[6:0]), .in1(raddr[6:0]), .out(multiplexer_4_out), .sel(decoder_1_out1));
  Multiplexer #(.enable("false")) multiplexer_5 (.in0(1'b0), .in1(decoder_1_out1), .out(multiplexer_5_out), .sel(ren));
  Register #(.width(1)) rb (.D(multiplexer_5_out), .Q(rb_q), .clk(clk));  // open: en, clr
  Register #(.width(1)) wa (.D(multiplexer_3_out), .Q(wa_q), .clk(clk));  // open: en, clr
  Register #(.width(1)) dren (.D(ren), .Q(dren_q), .clk(clk));  // open: en, clr
  Multiplexer #(.width(7), .enable("false")) multiplexer_6 (
    .in0(waddr[6:0]), .in1(raddr[6:0]), .out(multiplexer_6_out), .sel(decoder_1_out2));
  Multiplexer #(.enable("false")) multiplexer_7 (.in0(1'b0), .in1(decoder_1_out2), .out(multiplexer_7_out), .sel(ren));
  Register #(.width(1)) wb (.D(multiplexer_8_out), .Q(wb_q), .clk(clk));  // open: en, clr
  Multiplexer #(.enable("false")) multiplexer_8 (
    .in0(1'b0), .in1(decoder_2_out1), .out(multiplexer_8_out), .sel(and_1_out));
  Register #(.width(2)) drmem (.D(raddr[8:7]), .Q(drmem_q), .clk(clk));  // open: en, clr
  Register #(.width(7)) addrc (.D(multiplexer_6_out), .Q(addrc_q), .clk(clk));  // open: en, clr
  Register #(.width(1)) rc (.D(multiplexer_7_out), .Q(rc_q), .clk(clk));  // open: en, clr
  Multiplexer #(.enable("false")) multiplexer_9 (
    .in0(1'b0), .in1(decoder_2_out2), .out(multiplexer_9_out), .sel(and_1_out));
  Multiplexer #(.width(7), .enable("false")) multiplexer_10 (
    .in0(waddr[6:0]), .in1(raddr[6:0]), .out(multiplexer_10_out), .sel(decoder_1_out3));
  Register #(.width(7)) addrd (.D(multiplexer_10_out), .Q(addrd_q), .clk(clk));  // open: en, clr
  Register #(.width(1)) rd (.D(multiplexer_11_out), .Q(rd_q), .clk(clk));  // open: en, clr
  Multiplexer #(.enable("false")) multiplexer_11 (
    .in0(1'b0), .in1(decoder_1_out3), .out(multiplexer_11_out), .sel(ren));
  Register #(.width(1)) wc (.D(multiplexer_9_out), .Q(wc_q), .clk(clk));  // open: en, clr
  Register #(.width(1)) wd (.D(multiplexer_12_out), .Q(wd_q), .clk(clk));  // open: en, clr
  Multiplexer #(.enable("false")) multiplexer_12 (
    .in0(1'b0), .in1(decoder_2_out3), .out(multiplexer_12_out), .sel(and_1_out));
  RAM #(.addrWidth(7)) ram_1 (.addr(addra_q), .data(ram_1_data), .clk(clk), .ld(wa_q));  // open: sel, clr
  RAM #(.addrWidth(7)) ram_2 (.addr(addrb_q), .data(ram_2_data), .clk(clk), .ld(wb_q));  // open: sel, clr
  RAM #(.addrWidth(7)) ram_3 (.addr(addrc_q), .data(ram_3_data), .clk(clk), .ld(wc_q));  // open: sel, clr
  RAM #(.addrWidth(7)) ram_4 (.addr(addrd_q), .data(ram_4_data), .clk(clk), .ld(wd_q));  // open: sel, clr
  Multiplexer #(.width(8), .enable("false")) multiplexer_13 (.in0(undriven_4), .in1(din), .out(ram_1_data), .sel(ra_q));
  Multiplexer #(.width(8), .enable("false")) multiplexer_14 (.in0(undriven_3), .in1(din), .out(ram_2_data), .sel(rb_q));
  Multiplexer #(.width(8), .enable("false")) multiplexer_15 (.in0(undriven_2), .in1(din), .out(ram_3_data), .sel(rc_q));
  Multiplexer #(.width(8), .enable("false")) multiplexer_16 (.in0(undriven), .in1(din), .out(ram_4_data), .sel(rd_q));
  Multiplexer #(.select(2), .width(8), .enable("false")) multiplexer_17 (
    .in0(undriven_4), .in1(undriven_3), .in2(undriven_2), .in3(undriven), .out(multiplexer_17_out),
    .sel(drmem_q));
  Multiplexer #(.width(8), .enable("false")) multiplexer_18 (
    .in0({8{1'b0}}), .in1(multiplexer_17_out), .out(dout), .sel(dren_q));
endmodule

module Multi_Bank_Memory (
  input  clk,
  input  ren,
  input  wen,
  input  [10:0] raddr,
  input  [10:0] waddr,
  input  [7:0] din,
  output [7:0] dout
);

  wire and_1_out, decoder_1_out0, decoder_1_out1, decoder_1_out2, decoder_1_out3, decoder_2_out0,
       decoder_2_out1, decoder_2_out2, decoder_2_out3, dren_q, multiplexer_1_out, multiplexer_2_out,
       multiplexer_3_out, multiplexer_4_out, multiplexer_5_out, multiplexer_6_out, multiplexer_7_out,
       multiplexer_8_out, nand_1_out, ra_q, rb_q, rd_q, wa_q, wb_q, wc_q, wd_q;
  wire [1:0] drbank_q, xnor_1_out;
  wire [7:0] a_dout, b_dout, c_dout, d_dout, multiplexer_9_out;

  Decoder #(.select(2), .enable("false")) decoder_1 (
    .out0(decoder_1_out0), .out1(decoder_1_out1), .out2(decoder_1_out2), .out3(decoder_1_out3),
    .sel(raddr[10:9]));
  Decoder #(.select(2), .enable("false")) decoder_2 (
    .out0(decoder_2_out0), .out1(decoder_2_out1), .out2(decoder_2_out2), .out3(decoder_2_out3),
    .sel(waddr[10:9]));
  assign xnor_1_out = ~(raddr[10:9] ^ waddr[10:9]);  // XNOR_Gate xnor_1, 2 bits wide
  Multiplexer #(.enable("false")) multiplexer_1 (.in0(1'b0), .in1(decoder_1_out0), .out(multiplexer_1_out), .sel(ren));
  Register #(.width(1)) ra (.D(multiplexer_1_out), .Q(ra_q), .clk(clk));  // open: en, clr
  nand nand_1 (nand_1_out, ren, xnor_1_out[0], xnor_1_out[1]);
  Multiplexer #(.enable("false")) multiplexer_2 (.in0(1'b0), .in1(decoder_1_out1), .out(multiplexer_2_out), .sel(ren));
  Multiplexer #(.enable("false")) multiplexer_3 (
    .in0(1'b0), .in1(decoder_2_out0), .out(multiplexer_3_out), .sel(and_1_out));
  and and_1 (and_1_out, wen, nand_1_out);
  Register #(.width(1)) rb (.D(multiplexer_2_out), .Q(rb_q), .clk(clk));  // open: en, clr
  Register #(.width(1)) wa (.D(multiplexer_3_out), .Q(wa_q), .clk(ren));  // open: en, clr
  Register #(.width(1)) dren (.D(ren), .Q(dren_q), .clk(ren));  // open: en, clr
  Multiplexer #(.enable("false")) multiplexer_4 (
    .in0(decoder_1_out2), .in1(decoder_1_out2), .out(multiplexer_4_out), .sel(ren));
  Register #(.width(1)) rc (.D(multiplexer_4_out), .Q(decoder_2_out2), .clk(clk));  // open: en, clr
  Register #(.width(1)) wb (.D(multiplexer_5_out), .Q(wb_q), .clk(ren));  // open: en, clr
  Multiplexer #(.enable("false")) multiplexer_5 (
    .in0(1'b0), .in1(decoder_2_out1), .out(multiplexer_5_out), .sel(and_1_out));
  Register #(.width(2)) drbank (.D(raddr[10:9]), .Q(drbank_q), .clk(ren));  // open: en, clr
  Multiplexer #(.enable("false")) multiplexer_6 (.in0(1'b0), .in1(decoder_1_out3), .out(multiplexer_6_out), .sel(ren));
  Multiplexer #(.enable("false")) multiplexer_7 (
    .in0(1'b0), .in1(decoder_2_out2), .out(multiplexer_7_out), .sel(and_1_out));
  Register #(.width(1)) rd (.D(multiplexer_6_out), .Q(rd_q), .clk(clk));  // open: en, clr
  Register #(.width(1)) wc (.D(multiplexer_7_out), .Q(wc_q), .clk(ren));  // open: en, clr
  Register #(.width(1)) wd (.D(multiplexer_8_out), .Q(wd_q), .clk(ren));  // open: en, clr
  Multiplexer #(.enable("false")) multiplexer_8 (
    .in0(1'b0), .in1(decoder_2_out3), .out(multiplexer_8_out), .sel(and_1_out));
  Bank a (.clk(clk), .ren(ra_q), .wen(wa_q), .raddr(waddr[8:0]), .waddr(raddr[8:0]), .din(din), .dout(a_dout));
  Bank b (.clk(clk), .ren(rb_q), .wen(wb_q), .raddr(waddr[8:0]), .waddr(raddr[8:0]), .din(din), .dout(b_dout));
  Bank c (
    .clk(clk), .ren(decoder_2_out2), .wen(wc_q), .raddr(waddr[8:0]), .waddr(raddr[8:0]), .din(din),
    .dout(c_dout));
  Bank d (.clk(clk), .ren(rd_q), .wen(wd_q), .raddr(waddr[8:0]), .waddr(raddr[8:0]), .din(din), .dout(d_dout));
  Multiplexer #(.select(2), .width(8), .enable("false")) multiplexer_9 (
    .in0(a_dout), .in1(b_dout), .in2(c_dout), .in3(d_dout), .out(multiplexer_9_out), .sel(drbank_q));
  Multiplexer #(.width(8), .enable("false")) multiplexer_10 (
    .in0({8{1'b0}}), .in1(multiplexer_9_out), .out(dout), .sel(dren_q));
  // also tied to GND on the sheet: decoder_1_out2
endmodule

module PPC (
  input  rst_n,
  input  enable,
  output direction,
  output [3:0] out
);

  wire clk_out, d_ff_1_q, d_ff_2_q, multiplexer_3_out, undriven_2, undriven_4;
  wire [2:0] undriven_3;
  wire [3:0] multiplexer_4_out, undriven, undriven_5, undriven_6;

  Clock clk (.out(clk_out));
  D_Flip_Flop d_ff_1 (.clk(multiplexer_3_out), .Q(d_ff_1_q), .preset(clk_out), .en(clk_out));  // open: D, Qn, reset
  D_Flip_Flop d_ff_2 (.Q(d_ff_2_q), .en(clk_out));  // open: clk, D, Qn, preset, reset
  Multiplexer #(.select(2), .width(4)) multiplexer_1 (
    .in0(4'b0000), .in1(4'b0000), .in3(undriven), .out(out), .en(enable));  // open: in2, sel
  Multiplexer #(.select(2)) multiplexer_2 (
    .in0(1'b1), .in1(1'b1), .in2(multiplexer_3_out), .out(direction), .en(enable));  // open: in3, sel
  max max_1 ();
  Multiplexer #(.select(3)) multiplexer_3 (
    .in0(undriven_2), .in4(1'b1), .out(multiplexer_3_out), .sel(undriven_3), .en(undriven_4));  // open: in1, in2, in3, in5, in6, in7
  min min_1 ();
  \else  else_1 ();
  minus minus_1 ();
  ADD add_1 ();
  Multiplexer #(.width(4)) multiplexer_4 (
    .in0(undriven_5), .in1(undriven_6), .out(multiplexer_4_out), .sel(multiplexer_3_out));  // open: en
endmodule

// +1'b1
module ADD (
);

  // AND_Gate and_1 is placed but not wired
endmodule

module PPPC (
  input  flip,
  input  max,
  input  min,
  input  enable,
  input  rst_n,
  output direction,
  output [3:0] out
);

  wire clk_out, d_ff_2_q, multiplexer_2_out, multiplexer_3_out, multiplexer_4_out, not_1_out, undriven,
       undriven_2, undriven_4, undriven_5, undriven_6, undriven_8, undriven_9;
  wire [3:0] undriven_3;
  wire [4:0] undriven_7;

  D_Flip_Flop d_ff_1 (.Qn(rst_n), .en(clk_out));  // open: clk, D, Q, preset, reset
  max_min max___min ();
  D_Flip_Flop d_ff_2 (.clk(multiplexer_4_out), .Q(d_ff_2_q), .en(clk_out));  // open: D, Qn, preset, reset
  Clock clk (.out(clk_out));
  Multiplexer #(.select(4)) multiplexer_1 (
    .in0(undriven_2), .in1(undriven_2), .in2(undriven_2), .in3(1'b1), .in4(undriven_2), .in5(undriven_2),
    .in6(undriven_2), .in7(undriven_2), .in9(undriven_5), .in10(undriven_5), .in11(undriven_5),
    .in12(undriven_5), .in13(undriven_5), .in14(undriven_5), .in15(undriven_5), .out(direction),
    .sel(undriven_3), .en(undriven_4));  // open: in8
  Multiplexer #(.select(4)) multiplexer_2 (
    .in0(min), .in1(min), .in2(min), .in3(min), .in4(min), .in5(min), .in6(min), .in7(min), .in9(undriven),
    .in10(undriven), .in11(undriven), .in12(undriven), .in13(undriven), .in14(undriven), .in15(undriven),
    .out(multiplexer_2_out), .sel(undriven_3), .en(undriven_4));  // open: in8
  not not_1 (not_1_out, direction);
  max_min max____out____min ();
  Multiplexer #(.select(5)) multiplexer_3 (
    .in0(undriven_6), .in1(undriven_6), .in2(undriven_6), .in3(undriven_6), .in4(1'b1), .in5(1'b1),
    .in6(1'b1), .in7(1'b1), .in8(1'b0), .in9(1'b0), .in10(1'b0), .in11(1'b0), .in12(1'b0), .in13(1'b0),
    .in14(1'b0), .in15(1'b0), .in16(undriven_6), .in17(undriven_6), .in18(undriven_6), .in19(not_1_out),
    .in20(undriven_6), .in21(undriven_6), .in22(undriven_6), .in23(not_1_out), .in24(undriven_6),
    .in25(undriven_6), .in26(undriven_6), .in27(not_1_out), .in28(undriven_6), .in29(undriven_6),
    .in30(undriven_6), .in31(not_1_out), .out(multiplexer_3_out), .sel(undriven_7), .en(undriven_3[0]));
  min min_1 ();
  max max_1 ();
  minus minus_1 ();
  ADD add_1 ();
  Multiplexer multiplexer_4 (
    .in0(undriven_8), .in1(undriven_9), .out(multiplexer_4_out), .sel(multiplexer_3_out));  // open: en
  // Pins of 1 and 4 bits meet at undriven_3
endmodule
