// Logisim project lab4_adv.circ as structural Verilog
module SDFF (
  input  clk,
  input  d,
  input  scan_in,
  input  rst_n,
  input  scan_en,
  output q
);

  wire multiplexer_1_out, multiplexer_2_out;

  Multiplexer #(.enable("false")) multiplexer_1 (
    .in0(1'b0), .in1(multiplexer_2_out), .out(multiplexer_1_out), .sel(rst_n));
  Multiplexer #(.enable("false")) multiplexer_2 (.in0(d), .in1(scan_in), .out(multiplexer_2_out), .sel(scan_en));
  D_Flip_Flop d_ff_1 (.clk(clk), .D(multiplexer_1_out), .Q(q));  // open: Qn, preset, en, reset
endmodule

module SCD (
  input  clk,
  input  scan_in,
  input  scan_en,
  input  rst_n,
  output scan_out
);

  wire [3:0] multiplier_1_cout, multiplier_1_out, sdff_4_q;
  wire [3:1] sdff_7_q;

  SDFF sdff_1 (
    .d(multiplier_1_out[0]), .scan_in(scan_in), .clk(clk), .scan_en(scan_en), .rst_n(rst_n), .q(sdff_4_q[3]));
  SDFF sdff_2 (
    .d(multiplier_1_out[1]), .scan_in(sdff_4_q[3]), .clk(clk), .scan_en(scan_en), .rst_n(rst_n),
    .q(sdff_4_q[2]));
  SDFF sdff_3 (
    .d(multiplier_1_out[2]), .scan_in(sdff_4_q[2]), .clk(clk), .scan_en(scan_en), .rst_n(rst_n),
    .q(sdff_4_q[1]));
  SDFF sdff_4 (
    .d(multiplier_1_out[3]), .scan_in(sdff_4_q[1]), .clk(clk), .scan_en(scan_en), .rst_n(rst_n),
    .q(sdff_4_q[0]));
  Multiplier #(.width(4)) multiplier_1 (
    .a(sdff_4_q), .b({sdff_7_q, scan_out}), .out(multiplier_1_out), .cout(multiplier_1_cout));  // open: cin
  SDFF sdff_5 (
    .d(multiplier_1_cout[0]), .scan_in(sdff_4_q[0]), .clk(clk), .scan_en(scan_en), .rst_n(rst_n),
    .q(sdff_7_q[3]));
  SDFF sdff_6 (
    .d(multiplier_1_cout[1]), .scan_in(sdff_7_q[3]), .clk(clk), .scan_en(scan_en), .rst_n(rst_n),
    .q(sdff_7_q[2]));
  SDFF sdff_7 (
    .d(multiplier_1_cout[2]), .scan_in(sdff_7_q[2]), .clk(clk), .scan_en(scan_en), .rst_n(rst_n),
    .q(sdff_7_q[1]));
  SDFF sdff_8 (
    .d(multiplier_1_cout[3]), .scan_in(sdff_7_q[1]), .clk(clk), .scan_en(scan_en), .rst_n(rst_n), .q(scan_out));
endmodule

module FibLFSR (
  input  clk,
  input  rst_n,
  output out
);
endmodule

module BIST (
  input  clk,
  input  rst_n,
  input  scan_en,
  output scan_in,
  output scan_out
);

  FibLFSR fiblfsr_1 (.clk(clk), .rst_n(rst_n), .out(scan_in));
  SCD scd_1 (.clk(clk), .scan_in(scan_in), .scan_en(scan_en), .rst_n(rst_n), .scan_out(scan_out));
endmodule
